# Fritzing sketch circuito01 (saved by Fritzing 1.0.5)

parts:
  LED_rojo = LED - 5mm [color="Red (633nm)" current=0.030A package="5 mm [THT]"]
  U1 = LIPO-1000mAh [package=lipo-1000]
  part = Resistor [tolerance=±5% power=0.25W resistance=220 package=THT]
  U2 = Battery Holders [package=lipo-1100mAh]

nets:
  (-)/S08: LED_rojo.cathode, U1.-
  R29/S07: LED_rojo.anode, part.Pin_0
  N1: U1.+, U2.-
  (+)/R30: part.Pin_1, U2.+
