# Fritzing sketch circuito03 (saved by Fritzing 1.0.5)

parts:
  U1 = LIPO-1000mAh [package=lipo-1000]
  R31 = Resistor [tolerance=±5% power=0.25W resistance=220 package=THT]
  U2 = Battery Holders [package=lipo-1100mAh]
  S9 = Pushbutton [package="[THT]"]
  R32 = Resistor [tolerance=±5% power=0.25W resistance=220 package=THT]
  S10 = Pushbutton [package="[THT]"]
  LED_verde = LED - 3mm [color="Green (570nm)" current=0.030A package="3 mm [THT]"]
  LED_amarillo = LED - 3mm [color="Yellow (595nm)" current=0.030A package="3 mm [THT]"]
  S11 = Pushbutton [package="[THT]"]
  S12 = Pushbutton [package="[THT]"]
  LED_rojo1 = LED - 3mm [color="Red (660nm)" current=0.030A package="3 mm [THT]"]
  LED_rojo2 = LED - 3mm [color="Red (660nm)" current=0.030A package="3 mm [THT]"]

nets:
  N1: U1.+, U2.-
  N2: U1.-, LED_verde.cathode, LED_amarillo.cathode, LED_rojo1.cathode, LED_rojo2.cathode
  N3: R31.Pin_0, S9.Pin_3, S9.Pin_4, S10.Pin_3, S10.Pin_4
  N4: R31.Pin_1, U2.+, R32.Pin_1
  N5: S9.Pin_1, S9.Pin_2, LED_amarillo.anode
  N6: R32.Pin_0, S11.Pin_3, S11.Pin_4, S12.Pin_3, S12.Pin_4
  N7: S10.Pin_1, S10.Pin_2, LED_verde.anode
  N8: S11.Pin_1, S11.Pin_2, LED_rojo1.anode
  N9: S12.Pin_1, S12.Pin_2, LED_rojo2.anode
