# Fritzing sketch circuito05 (saved by Fritzing 1.0.5)

parts:
  U1 = LIPO-1000mAh [package=lipo-1000]
  R31 = Resistor [tolerance=±5% power=0.25W resistance=120k package=THT]
  U2 = Battery Holders [package=lipo-1100mAh]
  R32 = Resistor [tolerance=±5% power=0.25W resistance=220 package=THT]
  S12 = Pushbutton [package="[THT]"]
  LED_rojo2 = LED - 3mm [color="Red (660nm)" current=0.030A package="3 mm [THT]"]
  Q1 = NPN-Transistor [package="TO92 [THT]"]
  C1 = Electrolytic Capacitor [capacitance=470µ voltage=10V package="100 mil [THT, electrolytic]"]

nets:
  N1: U1.+, U2.-
  N2: U1.-, Q1.E, C1.+
  N3: R31.Pin_0, S12.Pin_1, S12.Pin_2
  N4: R31.Pin_1, U2.+, R32.Pin_1
  N5: R32.Pin_0, LED_rojo2.anode
  N6: S12.Pin_3, S12.Pin_4, Q1.B, C1.-
  N7: LED_rojo2.cathode, Q1.C
